// Logisim project Computer.circ as structural Verilog: 6 circuits, main circuit ALU
module ALU (
  input  zx,
  input  nx,
  input  zy,
  input  ny,
  input  f,
  input  no,
  input  [15:0] x,
  input  [15:0] y,
  output [15:0] result,
  output zr,
  output ng
);

  wire or_1_out;
  wire [15:0] adder_1_out, and_1_out, and_2_out, and_3_out, bit_extender_1_out, bit_extender_2_out,
       enabledinverter_1_result, enabledinverter_2_result, multiplexer_1_out;

  assign bit_extender_1_out = {{15{zx}}, zx};  // Bit_Extender bit_extender_1
  assign bit_extender_2_out = {{15{zy}}, zy};  // Bit_Extender bit_extender_2
  // Probe on enabledinverter_1_result
  assign and_1_out = x & ~bit_extender_1_out;  // AND_Gate and_1, 16 bits wide
  assign and_2_out = y & ~bit_extender_2_out;  // AND_Gate and_2, 16 bits wide
  EnabledInverter enabledinverter_1 (.d(and_1_out), .en(nx), .result(enabledinverter_1_result));
  // Probe on enabledinverter_2_result
  EnabledInverter enabledinverter_2 (.d(and_2_out), .en(ny), .result(enabledinverter_2_result));
  assign and_3_out = enabledinverter_1_result & enabledinverter_2_result;  // AND_Gate and_3, 16 bits wide
  Adder #(.width(16)) adder_1 (
    .a(enabledinverter_1_result), .b(enabledinverter_2_result), .out(adder_1_out));  // open: cin, cout
  Multiplexer #(.width(16)) multiplexer_1 (.in0(and_3_out), .in1(adder_1_out), .out(multiplexer_1_out), .sel(f));
  EnabledInverter enabledinverter_3 (.d(multiplexer_1_out), .en(no), .result({ng, result[14:0]}));
  or or_1 (or_1_out, result[0], result[1], result[2], result[3], result[4], result[5], result[6], result[7], result[8], result[9], result[10], result[11], result[12], result[13], result[14], ng);
  not not_1 (zr, or_1_out);

  assign result[15] = ng;
endmodule

module JumpDecoder (
  input  zr,
  input  ng,
  input  [2:0] jump,
  input  opcode,
  output pcLoad,
  output pcInc
);

  wire and_1_out, and_2_out, and_3_out, and_4_out, and_5_out, and_6_out, and_7_out, and_8_out, and_9_out,
       and_10_out, or_1_out, or_2_out;

  and and_1 (and_1_out, jump[0], jump[1], ~jump[2], zr, opcode);  // AND_Gate
  and and_2 (and_2_out, jump[0], jump[1], ~jump[2], ~zr, ~ng, opcode);  // AND_Gate
  and and_3 (and_3_out, ~jump[0], jump[1], jump[2], zr, opcode);  // AND_Gate
  and and_4 (and_4_out, ~jump[0], jump[1], jump[2], ~zr, ng, opcode);  // AND_Gate
  or or_1 (or_1_out, and_1_out, and_2_out);
  or or_2 (or_2_out, and_3_out, and_4_out);
  and and_5 (and_5_out, opcode, ~jump[0], ~jump[1], ~jump[2]);  // AND_Gate
  and and_6 (and_6_out, jump[0], ~jump[1], ~jump[2], ~zr, ~ng, opcode);  // AND_Gate
  and and_7 (and_7_out, ~jump[0], jump[1], ~jump[2], zr, opcode);  // AND_Gate
  and and_8 (and_8_out, ~jump[0], ~jump[1], jump[2], ~zr, ng, opcode);  // AND_Gate
  and and_9 (and_9_out, jump[0], ~jump[1], jump[2], ~zr, opcode);  // AND_Gate
  and and_10 (and_10_out, opcode, jump[0], jump[1], jump[2]);
  or or_3 (pcLoad, and_6_out, and_7_out, or_1_out, and_8_out, and_9_out, or_2_out, and_10_out);
  or or_4 (pcInc, ~pcLoad, and_5_out);  // OR_Gate

  // Other names for the same wires on the sheet: j0 = jump[0]; j1 = jump[1]; j2 = jump[2]; op = opcode

  // Notes on the sheet:
  //   no jump
  //   greater than 0
  //   equal to zero
  //   greater than or equal to
  //   less than 0
  //   not equal to zero
  //   less than or equal to
  //   jump
  //   jump
endmodule

module InstructionDecoder (
  input  [15:0] instruction,
  output writeM,
  output dLoad,
  output aLoad,
  output no,
  output f,
  output ny,
  output zy,
  output nx,
  output zx,
  output amMuxSel
);

  and and_1 (writeM, instruction[15], instruction[3]);
  and and_2 (dLoad, instruction[15], instruction[4]);
  or or_1 (aLoad, ~instruction[15], instruction[5]);  // OR_Gate
  and and_3 (no, instruction[15], instruction[6]);
  and and_4 (f, instruction[15], instruction[7]);
  and and_5 (ny, instruction[15], instruction[8]);
  and and_6 (zy, instruction[15], instruction[9]);
  and and_7 (nx, instruction[15], instruction[10]);
  and and_8 (zx, instruction[15], instruction[11]);
  and and_9 (amMuxSel, instruction[15], instruction[12]);

  // Notes on the sheet:
  //   instruction: pull=down
  //   op code enable
endmodule

module CPU (
  input  [15:0] instruction,
  input  [15:0] inM,
  input  reset,
  input  clock,
  output writeM,
  output [15:0] D,
  output [15:0] outM,
  output [15:0] addressM,
  output [15:0] pc
);

  wire alu_1_ng, alu_1_zr, and_1_out, comparator_1_eq, d_ff_1_q, d_ff_2_q, instructiondecoder_1_aload,
       instructiondecoder_1_ammuxsel, instructiondecoder_1_dload, instructiondecoder_1_f,
       instructiondecoder_1_no, instructiondecoder_1_nx, instructiondecoder_1_ny, instructiondecoder_1_zx,
       instructiondecoder_1_zy, jumpdecoder_1_pcinc, jumpdecoder_1_pcload, not_1_out;
  wire [15:0] multiplexer_1_out, multiplexer_2_out;

  // Probe on instruction
  D_Flip_Flop #(.trigger("falling")) d_ff_1 (.D(reset), .clk(clock), .Q(d_ff_1_q));  // open: Qn, preset, reset
  D_Flip_Flop #(.trigger("falling")) d_ff_2 (
    .D(comparator_1_eq), .clk(clock), .Q(d_ff_2_q), .reset(d_ff_1_q));  // open: Qn, preset
  Comparator #(.width(16)) comparator_1 (.a(instruction), .b(16'h8000), .eq(comparator_1_eq));  // open: gt, lt
  and and_1 (and_1_out, ~d_ff_2_q, clock);  // AND_Gate
  JumpDecoder jumpdecoder_1 (
    .zr(alu_1_zr), .ng(alu_1_ng), .jump(instruction[2:0]), .opcode(instruction[15]),
    .pcLoad(jumpdecoder_1_pcload), .pcInc(jumpdecoder_1_pcinc));
  InstructionDecoder instructiondecoder_1 (
    .instruction(instruction), .writeM(writeM), .dLoad(instructiondecoder_1_dload),
    .aLoad(instructiondecoder_1_aload), .no(instructiondecoder_1_no), .f(instructiondecoder_1_f),
    .ny(instructiondecoder_1_ny), .zy(instructiondecoder_1_zy), .nx(instructiondecoder_1_nx),
    .zx(instructiondecoder_1_zx), .amMuxSel(instructiondecoder_1_ammuxsel));
  Multiplexer #(.width(16)) multiplexer_1 (.in0(outM), .in1(instruction), .out(multiplexer_1_out), .sel(not_1_out));
  not not_1 (not_1_out, instruction[15]);
  Register #(.width(16)) ARegister (
    .D(multiplexer_1_out), .en(instructiondecoder_1_aload), .clk(and_1_out), .Q(addressM), .clr(d_ff_1_q));
  Register #(.width(16)) DRegister (.D(outM), .en(instructiondecoder_1_dload), .clk(and_1_out), .Q(D), .clr(d_ff_1_q));
  Multiplexer #(.width(16)) multiplexer_2 (
    .in0(addressM), .in1(inM), .out(multiplexer_2_out), .sel(instructiondecoder_1_ammuxsel));
  Counter #(.max('hffff), .width(16)) ProgramCounter (
    .load(jumpdecoder_1_pcload), .D(addressM), .count(jumpdecoder_1_pcinc), .Q(pc), .clk(and_1_out),
    .clr(d_ff_1_q));  // open: carry, up
  ALU alu_1 (
    .zy(instructiondecoder_1_zy), .x(D), .y(multiplexer_2_out), .ny(instructiondecoder_1_ny),
    .f(instructiondecoder_1_f), .no(instructiondecoder_1_no), .zx(instructiondecoder_1_zx),
    .nx(instructiondecoder_1_nx), .zr(alu_1_zr), .ng(alu_1_ng), .result(outM));

  // Notes on the sheet:
  //   halt detect
  //   reset signal
  //   clock signal
endmodule

module System (
  input  reset
);

  wire clock_1_out, cpu_1_writem, MemoryReset_q;
  wire [15:0] cpu_1_addressm, cpu_1_d, cpu_1_outm, cpu_1_pc, DataMemory_dout, InstructionMemory_data,
       RightWrite_q;

  ROM #(.addrWidth(16), .dataWidth(16)) InstructionMemory (.addr(cpu_1_pc), .data(InstructionMemory_data));
  Clock clock_1 (.out(clock_1_out));
  D_Flip_Flop #(.trigger("falling")) MemoryReset (
    .D(reset), .clk(clock_1_out), .Q(MemoryReset_q));  // open: Qn, preset, reset
  CPU cpu_1 (
    .instruction(InstructionMemory_data), .inM(DataMemory_dout), .reset(reset), .clock(clock_1_out),
    .writeM(cpu_1_writem), .D(cpu_1_d), .outM(cpu_1_outm), .addressM(cpu_1_addressm), .pc(cpu_1_pc));
  // Probe on cpu_1_addressm
  // Probe on cpu_1_d
  Register #(.width(16)) RightWrite (
    .D(cpu_1_outm), .en(cpu_1_writem), .clk(clock_1_out), .Q(RightWrite_q), .clr(MemoryReset_q));
  RAM #(.addrWidth(16), .clearpin("true"), .dataWidth(16), .enables("line")) DataMemory (
    .addr(cpu_1_addressm), .we(cpu_1_writem), .clk(clock_1_out), .din(cpu_1_outm), .dout(DataMemory_dout),
    .clr(MemoryReset_q));
  // Probe on RightWrite_q

  // Notes on the sheet:
  //   contents of InstructionMemory (hex, n*v repeats v):
  //   0 fc10 1 ea88 2 efc8 0 fc10 20 e302 2 f010 1c e305 0 fc10 2 f4d0 0 e308 2 fc10 2 f088 0 fc10 6 ea87
  //   1 fdc8 e ea87 8000
endmodule

module EnabledInverter (
  input  en,
  input  [15:0] d,
  output [15:0] result
);

  wire [15:0] bit_extender_1_out;

  assign bit_extender_1_out = {{15{en}}, en};  // Bit_Extender bit_extender_1
  assign result = bit_extender_1_out ^ d;  // XOR_Gate xor_1, 16 bits wide
endmodule
