// Logisim project TestALU.circ as structural Verilog: 3 circuits, main circuit ALU
module ALU (
  input  zx,
  input  nx,
  input  zy,
  input  ny,
  input  f,
  input  no,
  input  [15:0] x,
  input  [15:0] y,
  output [15:0] result,
  output zr,
  output ng
);

  wire or_1_out;
  wire [15:0] adder_1_out, and_1_out, and_2_out, and_3_out, bit_extender_1_out, bit_extender_2_out,
       inabledinverter_1_result, inabledinverter_2_result, multiplexer_1_out, not_1_out;

  assign bit_extender_1_out = {{15{zx}}, zx};  // Bit_Extender bit_extender_1
  assign bit_extender_2_out = {{15{zy}}, zy};  // Bit_Extender bit_extender_2
  // Probe on inabledinverter_1_result
  assign and_1_out = x & ~bit_extender_1_out;  // AND_Gate and_1, 16 bits wide
  assign and_2_out = y & ~bit_extender_2_out;  // AND_Gate and_2, 16 bits wide
  inabledInverter inabledinverter_1 (.d(and_1_out), .en(nx), .result(inabledinverter_1_result));
  // Probe on inabledinverter_2_result
  inabledInverter inabledinverter_2 (.d(and_2_out), .en(ny), .result(inabledinverter_2_result));
  assign and_3_out = inabledinverter_1_result & inabledinverter_2_result;  // AND_Gate and_3, 16 bits wide
  Adder #(.width(16)) adder_1 (
    .a(inabledinverter_1_result), .b(inabledinverter_2_result), .out(adder_1_out));  // open: cin, cout
  Multiplexer #(.width(16)) multiplexer_1 (.in0(and_3_out), .in1(adder_1_out), .out(multiplexer_1_out), .sel(f));
  assign not_1_out = ~multiplexer_1_out;  // NOT_Gate not_1, 16 bits wide
  Multiplexer #(.width(16)) multiplexer_2 (
    .in0(multiplexer_1_out), .in1(not_1_out), .out({ng, result[14:0]}), .sel(no));
  or or_1 (or_1_out, result[0], result[1], result[2], result[3], result[4], result[5], result[6], result[7], result[8], result[9], result[10], result[11], result[12], result[13], result[14], ng);
  not not_2 (zr, or_1_out);

  assign result[15] = ng;
endmodule

module ALUTest (
);

  wire button_1_out, clock_1_out, comparator_1_eq, d_ff_1_q, not_1_out;
  wire [1:0] alu_1_ng;
  wire [5:0] ControlInputROM_data, counter_1_q;
  wire [15:0] alu_1_result, XInputROM_data, YInputRom_data;
  wire [17:0] OutputRom_data;

  Counter #(.max('h23), .width(6)) counter_1 (
    .Q(counter_1_q), .clk(clock_1_out), .clr(button_1_out));  // open: load, D, count, carry, up
  Clock clock_1 (.out(clock_1_out));
  Button button_1 (.out(button_1_out));
  ROM #(.addrWidth(6), .dataWidth(6)) ControlInputROM (.addr(counter_1_q), .data(ControlInputROM_data));
  ROM #(.addrWidth(6), .dataWidth(16)) XInputROM (.addr(counter_1_q), .data(XInputROM_data));
  ROM #(.addrWidth(6), .dataWidth(16)) YInputRom (.addr(counter_1_q), .data(YInputRom_data));
  ROM #(.addrWidth(6), .dataWidth(18)) OutputRom (.addr(counter_1_q), .data(OutputRom_data));
  ALU alu_1 (
    .zy(ControlInputROM_data[3]), .x(XInputROM_data), .y(YInputRom_data), .ny(ControlInputROM_data[2]),
    .f(ControlInputROM_data[1]), .no(ControlInputROM_data[0]), .zx(ControlInputROM_data[5]),
    .nx(ControlInputROM_data[4]), .zr(alu_1_ng[1]), .ng(alu_1_ng[0]), .result(alu_1_result));
  not not_1 (not_1_out, comparator_1_eq);
  Comparator #(.mode("unsigned"), .width(18)) comparator_1 (
    .a({alu_1_result, alu_1_ng}), .b(OutputRom_data), .eq(comparator_1_eq));  // open: gt, lt
  D_Flip_Flop d_ff_1 (.D(not_1_out), .clk(clock_1_out), .Q(d_ff_1_q));  // open: Qn, preset, reset
  Counter #(.ongoal("stay")) counter_2 (
    .count(d_ff_1_q), .clk(clock_1_out), .clr(button_1_out));  // open: load, D, Q, carry, up

  // Notes on the sheet:
  //   contents of ControlInputROM (hex, n*v repeats v):
  //   2a 3f 3a c 30 d 31 f 33 1f 37 e 32 2 13 7 0 15 2a 3f 3a c 30 d 31 f 33 1f 37 e 32 2 13 7 0 15
  //   contents of XInputROM (hex, n*v repeats v):
  //   18*0 18*11
  //   contents of YInputRom (hex, n*v repeats v):
  //   18*ffff 18*3
  //   contents of OutputRom (hex, n*v repeats v):
  //   2 4 3fffd 2 3fffd 3fffd 2 2 4 4 2 3fffd 3fff9 3fffd 4 3fffd 2 3fffd 2 4 3fffd 44 c 3ffb9 3fff1 3ffbd
  //   3fff5 48 10 40 8 50 38 3ffc9 4 4c
  //   Reset
  //   Error Counter
endmodule

module inabledInverter (
  input  en,
  input  [15:0] d,
  output [15:0] result
);

  wire [15:0] bit_extender_1_out;

  assign bit_extender_1_out = {{15{en}}, en};  // Bit_Extender bit_extender_1
  assign result = bit_extender_1_out ^ d;  // XOR_Gate xor_1, 16 bits wide
endmodule
